// Digital circuit SAP_git.dig as structural Verilog
module SAP_git (
  input  CLK,
  output [7:0] Data_BUS,
  output [3:0] Address_BUS,
  output [7:0] A,
  output [7:0] B,
  output [7:0] PC,
  output C,
  output Z,
  output [3:0] OPCODE
);

  wire alu_git_1_c, alu_git_1_z, and_2_out, cc_git_1_p2, control_git_1_p2, control_git_1_p3,
       control_git_1_p4, control_git_1_p5, control_git_1_p6, control_git_1_p7, control_git_1_p8,
       control_git_1_p9, control_git_1_p10, control_git_1_p11, control_git_1_p12, control_git_1_p13,
       control_git_1_p14, control_git_1_p15, not_1_out;
  wire [2:0] cc_git_1_p5;
  wire [3:0] ir_git_1_p4, multiplexer_2_out;
  wire [7:0] alu_git_1_s, multiplexer_1_out, rom_1_d;

  not not_1 (not_1_out, control_git_1_p2);
  // CC_git cc_git_1: pin names not known; wires that end beside it: 1'b1, cc_git_1_p2, cc_git_1_p5[0], cc_git_1_p5[1], cc_git_1_p5[2]
  and and_1 (cc_git_1_p2, CLK, not_1_out);
  // Control_git control_git_1: pin names not known; wires that end beside it: {Z, C, OPCODE, cc_git_1_p5}, control_git_1_p2, control_git_1_p3, control_git_1_p4, control_git_1_p5, control_git_1_p6, control_git_1_p7, control_git_1_p8, control_git_1_p9, control_git_1_p10, control_git_1_p11, control_git_1_p12, control_git_1_p13, control_git_1_p14, control_git_1_p15
  FLAG_git flag_git_1 (.CLK(cc_git_1_p2), .en(control_git_1_p14), .Z(alu_git_1_c), .C(alu_git_1_z), .Z_2(Z), .C_2(C));
  // RegisterA_git registera_git_1: pin names not known; wires that end beside it: Data_BUS, cc_git_1_p2, control_git_1_p7, A
  // PC_git pc_git_1: pin names not known; wires that end beside it: cc_git_1_p2, control_git_1_p11, cc_git_1_p2, control_git_1_p13, Data_BUS, PC
  and and_2 (and_2_out, control_git_1_p5, control_git_1_p7);
  // IR_git ir_git_1: pin names not known; wires that end beside it: Data_BUS, cc_git_1_p2, control_git_1_p6, {OPCODE, ir_git_1_p4}
  assign Data_BUS = control_git_1_p12 ? PC : 8'bz;  // Driver driver_1
  assign Data_BUS = control_git_1_p15 ? A : 8'bz;  // Driver driver_2
  RegisterB_git registerb_git_1 (.B(Data_BUS), .CLK(cc_git_1_p2), .B_in(control_git_1_p10), .B_2(B));
  // MAR_git mar_git_1: pin names not known; wires that end beside it: Data_BUS, cc_git_1_p2, control_git_1_p3, Address_BUS
  Multiplexer #(.Bits(8)) multiplexer_1 (.sel(control_git_1_p8), .in_0(B), .in_1({8{1'b0}}), .out(multiplexer_1_out));
  ROM #(.AddrBits(4), .Bits(8)) rom_1 (.A(Address_BUS), .sel(1'b1), .D(rom_1_d));
  ALU_git alu_git_1 (
    .B(multiplexer_1_out), .A(A), .SUB(control_git_1_p9), .C(alu_git_1_c), .Z(alu_git_1_z), .S(alu_git_1_s));
  Multiplexer #(.Bits(4)) multiplexer_2 (.sel(and_2_out), .in_0(OPCODE), .in_1(4'b0000), .out(multiplexer_2_out));
  assign Data_BUS = control_git_1_p4 ? rom_1_d : 8'bz;  // Driver driver_3
  assign Data_BUS = control_git_1_p5 ? {multiplexer_2_out, ir_git_1_p4} : 8'bz;  // Driver driver_4
  assign Data_BUS = control_git_1_p8 ? alu_git_1_s : 8'bz;  // Driver driver_5

  // Notes on the sheet:
  //   CLK: Hz: 2
  //   contents of rom_1 (hex, n*v repeats v):
  //   1f,3e,88,76,51,f0,53,f0,52,f0,4*0,8,8
endmodule
